# Fritzing sketch Dice (saved by Fritzing 0.9.3b)
circuit board: 8.46667cm x 5.64444cm
breadboards: 1

parts:
  Bauteil1 = Arduino Uno (Rev3)
  LED1 = LED - 5mm [color="Red (633nm)" package="5 mm [THT]"]
  LED2 = LED - 5mm [color="Red (633nm)" package="5 mm [THT]"]
  LED3 = LED - 5mm [color="Red (633nm)" package="5 mm [THT]"]
  LED4 = LED - 5mm [color="Red (633nm)" package="5 mm [THT]"]
  LED5 = LED - 5mm [color="Red (633nm)" package="5 mm [THT]"]
  LED6 = LED - 5mm [color="Red (633nm)" package="5 mm [THT]"]
  S1 = Pushbutton [package="[THT]"]
  R1 = Resistor [tolerance=±5% resistance=100 package=THT]
  R2 = Resistor [tolerance=±5% resistance=100 package=THT]
  R3 = Resistor [tolerance=±5% resistance=100 package=THT]
  R4 = Resistor [tolerance=±5% resistance=100 package=THT]
  R5 = Resistor [tolerance=±5% resistance=100 package=THT]
  R6 = Resistor [tolerance=±5% resistance=100 package=THT]
  R7 = Resistor [tolerance=±5% resistance=100k package=THT]

nets:
  N1: Bauteil1.D8, LED6.anode
  N2: Bauteil1.D12/MISO, S1.Pin_3, S1.Pin_4, R7.Pin_1
  N3: Bauteil1.D3_PWM, LED1.anode
  N4: Bauteil1.D4, LED2.anode
  N5: Bauteil1.D5_PWM, LED3.anode
  N6: Bauteil1.D6_PWM, LED4.anode
  N7: Bauteil1.D7, LED5.anode
  N8: Bauteil1.5V, S1.Pin_1, S1.Pin_2
  N9: Bauteil1.GND, R1.Pin_1, R2.Pin_1, R3.Pin_1, R4.Pin_1, R5.Pin_1, R6.Pin_1, R7.Pin_0
  N10: LED1.cathode, R1.Pin_0
  N11: LED2.cathode, R2.Pin_0
  N12: LED3.cathode, R3.Pin_0
  N13: LED4.cathode, R4.Pin_0
  N14: LED5.cathode, R5.Pin_0
  N15: LED6.cathode, R6.Pin_0
